// Logisim project Mark1Computer.circ as structural Verilog
module abstracted (
);

  wire and_1_out, and_2_out, and_3_out, and_4_out, and_5_out, and_6_out, and_7_out, and_8_out, and_9_out,
       and_10_out, and_11_out, and_12_out, and_13_out, and_14_out, and_15_out, and_16_out, and_18_out,
       and_19_out, and_20_out, and_21_out, and_22_out, and_23_out, and_24_out, and_25_out, and_26_out,
       and_27_out, and_28_out, and_29_out, and_30_out, and_31_out, and_32_out, and_33_out, buffer_1_out,
       buffer_2_out, buffer_3_out, buffer_4_out, buffer_5_out, buffer_6_out, buffer_7_out, buffer_8_out,
       button_1_out, clock_1_out, d_ff_1_q, decoder_1_out1, decoder_1_out2, decoder_1_out3, decoder_1_out4,
       decoder_1_out5, decoder_1_out6, decoder_1_out7, decoder_2_out0, decoder_2_out1, decoder_2_out2,
       decoder_2_out3, decoder_3_out0, decoder_3_out1, decoder_3_out2, decoder_3_out3, decoder_4_out0,
       decoder_4_out1, decoder_4_out2, decoder_4_out7, decoder_4_out8, decoder_4_out9, decoder_4_out10,
       decoder_4_out11, decoder_4_out12, decoder_4_out13, decoder_4_out14, decoder_4_out15, decoder_5_out2,
       decoder_5_out3, decoder_5_out4, decoder_5_out5, decoder_6_out7, FS, IAE, IAS, IRE, IRS, MAE, MAS, MIE,
       MIS, MOE, MOS, not_1_out, or_1_out, or_2_out, or_3_out, or_4_out, or_7_out, or_8_out, or_9_out,
       or_10_out, or_11_out, or_12_out, or_13_out, or_14_out, PCC, PCE, PCS, pull_resistor_9_node, RR, RW;
  wire [2:0] pull_resistor_1_node_2, pull_resistor_2_node, STEP;
  wire [3:0] counter_3_q, counter_3_q_2, FLAG, nor_1_out;
  wire [3:3] or_5_out, pull_resistor_8_node;
  wire [7:0] AC, adder_1_out, ADDR, and_17_out, bit_extender_1_out, controlled_buffer_1_out,
       controlled_buffer_5_out, controlled_buffer_6_out, DATA, IA_q, IR, MAR, MDI, MDO, not_2_out, or_6_out,
       PC, pull_resistor_1_node, pull_resistor_5_node, pull_resistor_6_node, pull_resistor_7_node,
       ram_1_dout, RX, RY, RZ, T1_q, T2_q, TA_q, xor_1_out, xor_2_out;

  Register #(.trigger("high")) InstReg (.D(DATA), .en(decoder_1_out1), .clk(decoder_1_out1), .Q(IR));  // open: clr
  or or_1 (or_1_out, decoder_1_out2, decoder_1_out3, decoder_1_out4, decoder_1_out6, decoder_1_out7, decoder_1_out5);
  Counter counter_1 (
    .load(PCS), .up(1'b1), .count(PCC), .clk(and_1_out), .D(controlled_buffer_1_out), .Q(PC));  // open: clr, carry
  assign controlled_buffer_1_out = PCS ? ADDR : 8'bz;  // Controlled_Buffer controlled_buffer_1
  Pull_Resistor pull_resistor_1 (.node({pull_resistor_1_node[7], pull_resistor_1_node_2, pull_resistor_1_node[3:0]}));
  assign {pull_resistor_1_node[7], pull_resistor_1_node_2, pull_resistor_1_node[3:0]} = or_1_out ? IR : 8'bz;  // Controlled_Buffer controlled_buffer_2
  Decoder #(.enable("false"), .select(3)) decoder_1 (
    .out1(decoder_1_out1), .out2(decoder_1_out2), .out3(decoder_1_out3), .out4(decoder_1_out4),
    .out5(decoder_1_out5), .out6(decoder_1_out6), .out7(decoder_1_out7), .sel(STEP));  // open: out0
  Button button_1 (.out(button_1_out));
  not not_1 (not_1_out, decoder_4_out7);
  Clock clock_1 (.out(clock_1_out));
  D_Flip_Flop d_ff_1 (.D(not_1_out), .clk(clock_1_out), .Q(d_ff_1_q), .reset(button_1_out));  // open: Qn, preset
  Register #(.trigger("high")) IA (.D(DATA), .en(IAS), .clk(IAS), .Q(IA_q));  // open: clr
  ROM #(.dataWidth(16)) rom_1 (
    .addr({pull_resistor_1_node[7], pull_resistor_1_node_2, or_5_out[3], STEP}),
    .data({PCC, PCE, PCS, IAS, IAE, MAS, MAE, MIS, MIE, MOS, MOE, RR, RW, IRS, IRE, FS}));
  and and_1 (and_1_out, clock_1_out, d_ff_1_q);
  Pull_Resistor pull_resistor_2 (.node(pull_resistor_2_node));
  Pull_Resistor pull_resistor_3 (.node(ADDR));
  assign ADDR = IAE ? IA_q : 8'bz;  // Controlled_Buffer controlled_buffer_3
  assign ADDR = PCE ? PC : 8'bz;  // Controlled_Buffer controlled_buffer_4
  Counter #(.max('h7), .trigger("falling"), .width(3)) counter_2 (
    .clr(button_1_out), .load(1'b0), .count(1'b1), .clk(and_1_out), .D(pull_resistor_2_node), .Q(STEP));  // open: up, carry
  Register #(.trigger("high")) u_MAR (.D(ADDR), .en(MAS), .clk(MAS), .Q(MAR));  // open: clr
  Register #(.trigger("high")) u_MDI (.D(DATA), .en(MIS), .clk(MIS), .Q(MDI));  // open: clr
  RAM #(.trigger("high"), .\type ("nonvolatile")) ram_1 (
    .addr(controlled_buffer_5_out), .we(RW), .oe(RR), .din(controlled_buffer_6_out), .dout(ram_1_dout));
  assign controlled_buffer_5_out = MAE ? MAR : 8'bz;  // Controlled_Buffer controlled_buffer_5
  assign controlled_buffer_6_out = MIE ? MDI : 8'bz;  // Controlled_Buffer controlled_buffer_6
  LED led_1 (.in(PCC));
  Decoder #(.enable("false"), .select(2)) decoder_2 (
    .out0(decoder_2_out0), .out1(decoder_2_out1), .out2(decoder_2_out2), .out3(decoder_2_out3),
    .sel(pull_resistor_1_node[3:2]));
  Decoder #(.enable("false"), .select(2)) decoder_3 (
    .out0(decoder_3_out0), .out1(decoder_3_out1), .out2(decoder_3_out2), .out3(decoder_3_out3),
    .sel(pull_resistor_1_node[1:0]));
  Decoder #(.enable("false"), .select(4)) decoder_4 (
    .out0(decoder_4_out0), .out1(decoder_4_out1), .out2(decoder_4_out2), .out7(decoder_4_out7),
    .out8(decoder_4_out8), .out9(decoder_4_out9), .out10(decoder_4_out10), .out11(decoder_4_out11),
    .out12(decoder_4_out12), .out13(decoder_4_out13), .out14(decoder_4_out14), .out15(decoder_4_out15),
    .sel({pull_resistor_1_node[7], pull_resistor_1_node_2}));  // open: out3, out4, out5, out6
  Decoder #(.enable("false"), .select(3)) decoder_5 (
    .out2(decoder_5_out2), .out3(decoder_5_out3), .out4(decoder_5_out4), .out5(decoder_5_out5), .sel(STEP));  // open: out0, out1, out6, out7
  LED led_2 (.in(PCE));
  LED led_3 (.in(PCS));
  or or_2 (or_2_out, decoder_4_out8, decoder_4_out9, decoder_4_out10, decoder_4_out11, decoder_4_out13, decoder_4_out14, decoder_4_out15, decoder_4_out12);
  LED led_4 (.in(IAS));
  and and_2 (and_2_out, decoder_4_out2, decoder_5_out2);
  and and_3 (and_3_out, or_2_out, decoder_5_out3);
  and and_4 (and_4_out, or_2_out, decoder_5_out2);
  and and_5 (and_5_out, decoder_2_out0, FLAG[3]);
  and and_6 (and_6_out, decoder_2_out1, FLAG[2]);
  and and_7 (and_7_out, decoder_2_out2, FLAG[1]);
  and and_8 (and_8_out, decoder_2_out3, FLAG[0]);
  Register #(.trigger("high")) u_MDO (.D(ram_1_dout), .en(MOS), .clk(MOS), .Q(MDO));  // open: clr
  LED led_5 (.in(IAE));
  LED led_6 (.in(MAS));
  and and_9 (and_9_out, decoder_4_out0, decoder_5_out5);
  and and_10 (and_10_out, decoder_4_out1, decoder_5_out4);
  or or_3 (or_3_out, and_10_out, or_4_out);
  or or_4 (or_4_out, and_2_out, and_3_out);
  or or_5 (or_5_out[3], and_5_out, and_6_out, and_7_out, and_8_out);
  assign DATA = MOE ? MDO : 8'bz;  // Controlled_Buffer controlled_buffer_7
  Pull_Resistor pull_resistor_4 (.node(DATA));
  LED led_7 (.in(MAE));
  LED led_8 (.in(MIS));
  buf buffer_1 (buffer_1_out, or_3_out);
  buf buffer_2 (buffer_2_out, buffer_1_out);
  Register #(.trigger("high")) T1 (.D(DATA), .en(and_11_out), .clk(and_11_out), .Q(T1_q));  // open: clr
  Register #(.trigger("high")) T2 (.D(DATA), .en(and_12_out), .clk(and_12_out), .Q(T2_q));  // open: clr
  Register #(.trigger("high")) TA (.D(pull_resistor_7_node), .en(and_13_out), .clk(and_13_out), .Q(TA_q));  // open: clr
  LED led_9 (.in(MIE));
  buf buffer_3 (buffer_3_out, buffer_5_out);
  buf buffer_4 (buffer_4_out, buffer_2_out);
  buf buffer_5 (buffer_5_out, buffer_4_out);
  and and_11 (and_11_out, or_2_out, decoder_5_out3);
  and and_12 (and_12_out, or_2_out, decoder_5_out2);
  and and_13 (and_13_out, or_2_out, decoder_5_out4);
  and and_14 (and_14_out, or_2_out, decoder_5_out4);
  and and_15 (and_15_out, or_2_out, decoder_5_out4);
  and and_16 (and_16_out, or_2_out, ~decoder_4_out9, decoder_5_out5);  // AND_Gate
  Pull_Resistor pull_resistor_5 (.node(pull_resistor_5_node));
  assign pull_resistor_5_node = and_14_out ? T1_q : 8'bz;  // Controlled_Buffer controlled_buffer_8
  Pull_Resistor pull_resistor_6 (.node(pull_resistor_6_node));
  assign pull_resistor_6_node = and_15_out ? T2_q : 8'bz;  // Controlled_Buffer controlled_buffer_9
  Pull_Resistor pull_resistor_7 (.node(pull_resistor_7_node));
  assign DATA = and_16_out ? TA_q : 8'bz;  // Controlled_Buffer controlled_buffer_10
  LED led_10 (.in(MOS));
  LED led_11 (.in(MOE));
  buf buffer_6 (buffer_6_out, buffer_3_out);
  buf buffer_7 (buffer_7_out, buffer_6_out);
  buf buffer_8 (buffer_8_out, buffer_7_out);
  LED led_12 (.in(RR));
  assign bit_extender_1_out = {{7{decoder_4_out9}}, decoder_4_out9};  // Bit_Extender bit_extender_1
  Comparator #(.mode("unsigned")) comparator_1 (
    .a(pull_resistor_5_node), .b(pull_resistor_6_node), .gt(nor_1_out[2]), .eq(nor_1_out[1]));  // open: lt
  nor nor_1 (nor_1_out[0], pull_resistor_5_node[0], pull_resistor_5_node[1], pull_resistor_5_node[2], pull_resistor_5_node[3], pull_resistor_5_node[5], pull_resistor_5_node[6], pull_resistor_5_node[7], pull_resistor_5_node[4]);
  assign and_17_out = pull_resistor_5_node & pull_resistor_6_node;  // AND_Gate and_17, 8 bits wide
  assign or_6_out = pull_resistor_5_node | pull_resistor_6_node;  // OR_Gate or_6, 8 bits wide
  assign xor_1_out = pull_resistor_5_node ^ pull_resistor_6_node;  // XOR_Gate xor_1, 8 bits wide
  assign not_2_out = ~pull_resistor_5_node;  // NOT_Gate not_2, 8 bits wide
  LED led_13 (.in(RW));
  LED led_14 (.in(IRS));
  and and_18 (and_18_out, decoder_2_out0, and_9_out);
  and and_19 (and_19_out, decoder_2_out1, and_9_out);
  and and_20 (and_20_out, decoder_2_out2, and_9_out);
  and and_21 (and_21_out, decoder_2_out3, and_9_out);
  and and_22 (and_22_out, decoder_2_out0, buffer_8_out);
  and and_23 (and_23_out, decoder_2_out1, buffer_8_out);
  and and_24 (and_24_out, decoder_2_out2, buffer_8_out);
  and and_25 (and_25_out, decoder_2_out3, buffer_8_out);
  and and_26 (and_26_out, decoder_3_out0, and_2_out);
  and and_27 (and_27_out, decoder_3_out1, and_2_out);
  and and_28 (and_28_out, decoder_3_out2, and_2_out);
  and and_29 (and_29_out, decoder_3_out3, and_2_out);
  and and_30 (and_30_out, decoder_3_out0, and_4_out);
  and and_31 (and_31_out, decoder_3_out1, and_4_out);
  and and_32 (and_32_out, decoder_3_out2, and_4_out);
  and and_33 (and_33_out, decoder_3_out3, and_4_out);
  Adder adder_1 (.a(pull_resistor_5_node), .b(xor_2_out), .out(adder_1_out), .cin(decoder_4_out9), .cout(nor_1_out[3]));
  assign xor_2_out = pull_resistor_6_node ^ bit_extender_1_out;  // XOR_Gate xor_2, 8 bits wide
  Register #(.trigger("high"), .width(4)) FLAGS (
    .D(nor_1_out), .en(and_15_out), .clk(and_15_out), .Q(FLAG));  // open: clr
  LED led_15 (.in(IRE));
  LED led_16 (.in(FS));
  Multiplexer #(.select(3), .width(8)) multiplexer_1 (
    .in0(adder_1_out), .in1(adder_1_out), .in3(and_17_out), .in4(or_6_out), .in5(xor_1_out), .in6(not_2_out),
    .out(pull_resistor_7_node), .sel(pull_resistor_1_node_2));  // open: in2, in7
  or or_7 (or_7_out, and_18_out, and_16_out, and_26_out);
  or or_8 (or_8_out, and_19_out, and_27_out);
  or or_9 (or_9_out, and_20_out, and_28_out);
  or or_10 (or_10_out, and_21_out, and_29_out);
  or or_11 (or_11_out, and_22_out, and_30_out);
  or or_12 (or_12_out, and_23_out, and_31_out);
  or or_13 (or_13_out, and_24_out, and_32_out);
  or or_14 (or_14_out, and_25_out, and_33_out);
  Register #(.trigger("high")) u_AC (.D(DATA), .en(or_7_out), .clk(or_7_out), .Q(AC));  // open: clr
  Register #(.trigger("high")) u_RX (.D(DATA), .en(or_8_out), .clk(or_8_out), .Q(RX));  // open: clr
  Register #(.trigger("high")) u_RY (.D(DATA), .en(or_9_out), .clk(or_9_out), .Q(RY));  // open: clr
  Register #(.trigger("high")) u_RZ (.D(DATA), .en(or_10_out), .clk(or_10_out), .Q(RZ));  // open: clr
  assign DATA = or_11_out ? AC : 8'bz;  // Controlled_Buffer controlled_buffer_11
  assign DATA = or_12_out ? RX : 8'bz;  // Controlled_Buffer controlled_buffer_12
  assign DATA = or_13_out ? RY : 8'bz;  // Controlled_Buffer controlled_buffer_13
  assign DATA = or_14_out ? RZ : 8'bz;  // Controlled_Buffer controlled_buffer_14
  Hex_Digit_Display #(.decimalPoint("false")) hex_digit_display_1 (.value(AC[7:4]));
  Hex_Digit_Display #(.decimalPoint("false")) hex_digit_display_2 (.value(IR[7:4]));
  Hex_Digit_Display #(.decimalPoint("false")) hex_digit_display_3 (.value({pull_resistor_8_node[3], STEP}));
  Pull_Resistor pull_resistor_8 (.node({pull_resistor_8_node[3], STEP}));
  Hex_Digit_Display #(.decimalPoint("false")) hex_digit_display_4 (.value(AC[3:0]));
  Hex_Digit_Display #(.decimalPoint("false")) hex_digit_display_5 (.value(IR[3:0]));
  Pull_Resistor #(.pull(1)) pull_resistor_9 (.node(pull_resistor_9_node));
  Decoder #(.enable("false"), .select(3)) decoder_6 (
    .out7(decoder_6_out7), .sel(STEP));  // open: out0, out1, out2, out3, out4, out5, out6
  Hex_Digit_Display #(.decimalPoint("false")) hex_digit_display_6 (.value(RX[7:4]));
  Hex_Digit_Display #(.decimalPoint("false")) hex_digit_display_7 (.value(RX[3:0]));
  Hex_Digit_Display #(.decimalPoint("false")) hex_digit_display_8 (.value(PC[7:4]));
  Hex_Digit_Display #(.decimalPoint("false")) hex_digit_display_9 (.value(PC[3:0]));
  Counter #(.trigger("falling")) counter_3 (
    .up(1'b1), .count(1'b1), .clk(decoder_6_out7), .Q({counter_3_q_2, counter_3_q}));  // open: clr, load, D, carry
  Hex_Digit_Display #(.decimalPoint("false")) hex_digit_display_10 (.value(RY[7:4]));
  Hex_Digit_Display #(.decimalPoint("false")) hex_digit_display_11 (.value(MAR[7:4]));
  Hex_Digit_Display #(.decimalPoint("false")) hex_digit_display_12 (.value(RY[3:0]));
  Hex_Digit_Display #(.decimalPoint("false")) hex_digit_display_13 (.value(MAR[3:0]));
  Hex_Digit_Display #(.decimalPoint("false")) hex_digit_display_14 (.value(RZ[7:4]));
  Hex_Digit_Display #(.decimalPoint("false")) hex_digit_display_15 (.value(RZ[3:0]));
  Hex_Digit_Display #(.decimalPoint("false")) hex_digit_display_16 (.value(MDI[7:4]));
  Hex_Digit_Display #(.decimalPoint("false")) hex_digit_display_17 (.value(MDI[3:0]));
  Hex_Digit_Display #(.decimalPoint("false")) hex_digit_display_18 (.value(counter_3_q_2));
  Hex_Digit_Display #(.decimalPoint("false")) hex_digit_display_19 (.value(counter_3_q));
  Hex_Digit_Display #(.decimalPoint("false")) hex_digit_display_20 (.value(DATA[7:4]));
  Hex_Digit_Display #(.decimalPoint("false")) hex_digit_display_21 (.value(DATA[3:0]));
  Hex_Digit_Display #(.decimalPoint("false")) hex_digit_display_22 (.value(MDO[7:4]));
  Hex_Digit_Display #(.decimalPoint("false")) hex_digit_display_23 (.value(MDO[3:0]));
  Hex_Digit_Display #(.decimalPoint("false")) hex_digit_display_24 (.value(ADDR[7:4]));
  Hex_Digit_Display #(.decimalPoint("false")) hex_digit_display_25 (.value(FLAG));
  Hex_Digit_Display #(.decimalPoint("false")) hex_digit_display_26 (.value(ADDR[3:0]));

  // Notes on the sheet:
  //   PROGRAM COUNTER
  //   contents of rom_1 (hex, n*v repeats v):
  //   4650 24 c652 1022 e52 8022 2 2 4650 24 c652 1022 e52 8022 2 2 4650 24 c652 1022 d02 828a 2 2 4650 24
  //   c652 1022 d02 828a 2 2 4650 24 8002 5*2 4650 24 8002 5*2 4650 24 c652 1022 d02 828a 2 2 4650 24 c652
  //   1022 d02 828a 2 2 4650 24 c652 1022 e52 8022 2 2 4650 24 c652 1022 e52 8022 2 2 4650 24 c652 1022
  //   2802 2 2 2 4650 24 c652 1022 2802 2 2 2 4650 24 8002 5*2 4650 24 c652 1022 2802 2 2 2 4650 24 6*2
  //   4650 24 6*2 4650 24 8002 2 3 2 2 2 4650 24 8002 2 3 2 2 2 4650 24 8002 2 3 2 2 2 4650 24 8002 2 3 2
  //   2 2 4650 24 8002 2 3 2 2 2 4650 24 8002 2 3 2 2 2 4650 24 8002 2 3 2 2 2 4650 24 8002 2 3 2 2 2 4650
  //   24 8002 2 3 2 2 2 4650 24 8002 2 3 2 2 2 4650 24 8002 2 3 2 2 2 4650 24 8002 2 3 2 2 2 4650 24 8002
  //   2 3 2 2 2 4650 24 8002 2 3 2 2 2 4650 24 8002 2 3 2 2 2 4650 24 8002 2 3 2 2 2
  //   MARK 1 COMPUTER
  //   RANDOM ACCESS MEMORY
  //   REG1
  //   REG2
  //   REG OPCODES
  //   MAJOR FUNCTIONS EEPROM CONTROL LOGIC
  //   REGISTER/CONDITIONAL CONTROL LOGIC
  //   CLOCK STEPS
  //   FLAGS MATCH
  //   T1S
  //   T2S
  //   TAS
  //   T1E
  //   T2E
  //   TAE
  //   ARITHMETIC LOGIC UNIT
  //   SA
  //   SX
  //   SY
  //   SZ
  //   EA
  //   EX
  //   EY
  //   EZ
  //   REGISTER BANK
  //   GP REG CONTENTS
  //   CPU REG CONTENTS
  //   STEP
  //   BUS CONTENTS
endmodule

module logicgated (
  input  in_1,
  input  in_2,
  input  in_3,
  input  in_4,
  input  in_5,
  input  in_6,
  input  in_7,
  input  in_8,
  input  in_9,
  input  in_10,
  input  in_11,
  input  in_12,
  input  in_13,
  input  in_14,
  input  in_15,
  input  in_16,
  input  in_17,
  input  in_18,
  input  in_19,
  input  in_20,
  input  in_21,
  input  in_22,
  input  in_23,
  input  in_24,
  input  in_25,
  input  in_26,
  input  in_27,
  input  in_28,
  input  in_29,
  input  in_30,
  input  in_31,
  input  in_32,
  input  in_33
);

  wire xor_1_out, xor_2_out;

  xor xor_1 (xor_1_out, in_16, in_32);
  // AND_Gate and_1 has open pins: in0=in_16, in1=in_32, out=open
  xor xor_2 (xor_2_out, in_16, in_32);
  // XOR_Gate xor_3 has open pins: in0=in_33, in1=xor_2_out, out=open

  // Notes on the sheet:
  //   B Input
  //   A Input
endmodule
